// Logisim project 1-FLIP_FLOP_D_E_JK.circ as structural Verilog: 3 circuits, main circuit Flip-Flop-JK-MS
module Flip_Flop_JK_MS (
  input  PRESET,
  input  J,
  input  K,
  input  CLEAR,
  output Q,
  output nQ
);

  wire clock_1_out, nand_1_out, nand_2_out, nand_3_out, nand_4_out, nand_5_out, nand_6_out, not_1_out,
       not_2_out, not_3_out;

  Clock clock_1 (.out(clock_1_out));
  nand nand_1 (nand_1_out, nQ, J, clock_1_out);
  not not_1 (not_1_out, clock_1_out);
  nand nand_2 (nand_2_out, clock_1_out, K, Q);
  not not_2 (not_2_out, PRESET);
  not not_3 (not_3_out, CLEAR);
  nand nand_3 (nand_3_out, not_2_out, nand_1_out, nand_4_out);
  nand nand_4 (nand_4_out, nand_3_out, nand_2_out, not_3_out);
  nand nand_5 (nand_5_out, not_3_out, nand_3_out, not_1_out);
  nand nand_6 (nand_6_out, not_1_out, nand_4_out, not_2_out);
  nand nand_7 (Q, not_2_out, nand_5_out, nQ);
  nand nand_8 (nQ, Q, nand_6_out, not_3_out);

  // Notes on the sheet:
  //   Flip-Flop-JK, sensivel a borda de descida
endmodule

module Flip_Flop_D (
  input  Data,
  input  CLK,
  output Q,
  output nQ
);

  wire nand_1_out, nand_2_out, not_1_out;

  not not_1 (not_1_out, Data);
  nand nand_1 (nand_1_out, Data, CLK);
  nand nand_2 (nand_2_out, CLK, not_1_out);
  nand nand_3 (Q, nand_1_out, nQ);
  nand nand_4 (nQ, Q, nand_2_out);
endmodule

module Flip_Flop_D_MS (
  input  PRESET,
  input  D,
  input  CLEAR,
  output Q,
  output nQ
);

  wire clock_1_out, nand_1_out, nand_2_out, nand_3_out, nand_4_out, nand_5_out, nand_6_out, not_1_out,
       not_2_out, not_3_out, not_4_out;

  Clock clock_1 (.out(clock_1_out));
  not not_1 (not_1_out, D);
  nand nand_1 (nand_1_out, nQ, D, clock_1_out);
  not not_2 (not_2_out, clock_1_out);
  nand nand_2 (nand_2_out, clock_1_out, not_1_out, Q);
  not not_3 (not_3_out, PRESET);
  not not_4 (not_4_out, CLEAR);
  nand nand_3 (nand_3_out, not_3_out, nand_1_out, nand_4_out);
  nand nand_4 (nand_4_out, nand_3_out, nand_2_out, not_4_out);
  nand nand_5 (nand_5_out, not_4_out, nand_3_out, not_2_out);
  nand nand_6 (nand_6_out, not_2_out, nand_4_out, not_3_out);
  nand nand_7 (Q, not_3_out, nand_5_out, nQ);
  nand nand_8 (nQ, Q, nand_6_out, not_4_out);
endmodule
