// Logisim project 10-UNIDADE_LOGICA_ARITMETICA.circ as structural Verilog: 16 circuits, main circuit ULA
module ULA (
  input  [7:0] A,
  input  [7:0] B,
  input  [3:0] Operacao,
  input  C_B_in,
  output [7:0] Resultado,
  output OverFlow
);

  wire somador_8bits_1_cout, subtrator_8bits_1_bout;
  wire [7:0] and_1_out, deslocador_2bits_dir_1_out, deslocador_2bits_esq_1_out_2, nand_1_out, nor_1_out,
       not_1_out, or_1_out, somador_8bits_1_saida, subtrator_8bits_1_saida, xor_8bits_1_out_3;

  assign not_1_out = ~A;  // NOT_Gate not_1, 8 bits wide
  assign and_1_out = A & B;  // AND_Gate and_1, 8 bits wide
  assign or_1_out = A | B;  // OR_Gate or_1, 8 bits wide
  assign nor_1_out = ~(A | B);  // NOR_Gate nor_1, 8 bits wide
  assign nand_1_out = ~(A & B);  // NAND_Gate nand_1, 8 bits wide
  XOR_8BITS xor_8bits_1 (.A(A), .B(B), .out_3(xor_8bits_1_out_3));
  DESLOCADOR_2BITS_ESQ deslocador_2bits_esq_1 (.in_1(A), .out_2(deslocador_2bits_esq_1_out_2));
  DESLOCADOR_2BITS_DIR deslocador_2bits_dir_1 (.In(A), .Out(deslocador_2bits_dir_1_out));
  SOMADOR_8BITS somador_8bits_1 (
    .A(A), .B(B), .Saida(somador_8bits_1_saida), .Cout(somador_8bits_1_cout), .Cin(C_B_in));
  SUBTRATOR_8BITS subtrator_8bits_1 (
    .A(A), .B(B), .Bin(C_B_in), .Saida(subtrator_8bits_1_saida), .Bout(subtrator_8bits_1_bout));
  or or_2 (OverFlow, somador_8bits_1_cout, subtrator_8bits_1_bout);
  MUX_16X1_8BITS mux_16x1_8bits_1 (
    .in_1(and_1_out), .in_2(or_1_out), .in_3(not_1_out), .in_4(nor_1_out), .in_5(nand_1_out),
    .in_6(xor_8bits_1_out_3), .in_7(deslocador_2bits_esq_1_out_2), .in_8(deslocador_2bits_dir_1_out),
    .in_9(somador_8bits_1_saida), .in_10(subtrator_8bits_1_saida), .in_11(Operacao), .out_12(Resultado));
endmodule

module XOR_1BIT (
  input  A,
  input  B,
  output S
);

  wire and_1_out, and_2_out, not_1_out, not_2_out;

  and and_1 (and_1_out, A, not_1_out);
  not not_1 (not_1_out, B);
  not not_2 (not_2_out, A);
  and and_2 (and_2_out, not_2_out, B);
  or or_1 (S, and_1_out, and_2_out);
endmodule

module XOR_8BITS (
  input  [7:0] A,
  input  [7:0] B,
  output [7:0] out_3
);

  XOR_1BIT xor_1bit_1 (.A(A[7]), .B(B[7]), .S(out_3[7]));
  XOR_1BIT xor_1bit_2 (.A(A[6]), .B(B[6]), .S(out_3[6]));
  XOR_1BIT xor_1bit_3 (.A(A[5]), .B(B[5]), .S(out_3[5]));
  XOR_1BIT xor_1bit_4 (.A(A[4]), .B(B[4]), .S(out_3[4]));
  XOR_1BIT xor_1bit_5 (.A(A[3]), .B(B[3]), .S(out_3[3]));
  XOR_1BIT xor_1bit_6 (.A(A[2]), .B(B[2]), .S(out_3[2]));
  XOR_1BIT xor_1bit_7 (.A(A[1]), .B(B[1]), .S(out_3[1]));
  XOR_1BIT xor_1bit_8 (.A(A[0]), .B(B[0]), .S(out_3[0]));
endmodule

module SOMADOR (
  input  A,
  input  B,
  input  Cin,
  output Soma,
  output Cout
);

  wire and_1_out, and_2_out, xor_1bit_1_s;

  XOR_1BIT xor_1bit_1 (.A(A), .B(B), .S(xor_1bit_1_s));
  XOR_1BIT xor_1bit_2 (.A(xor_1bit_1_s), .B(Cin), .S(Soma));
  and and_1 (and_1_out, xor_1bit_1_s, Cin);
  and and_2 (and_2_out, A, B);
  or or_1 (Cout, and_1_out, and_2_out);
endmodule

module SOMADOR_8BITS (
  input  [7:0] A,
  input  [7:0] B,
  input  Cin,
  output [7:0] Saida,
  output Cout
);

  wire somador_1_cout, somador_2_cout, somador_3_cout, somador_4_cout, somador_5_cout, somador_6_cout,
       somador_7_cout;

  SOMADOR somador_1 (.A(A[0]), .B(B[0]), .Cin(Cin), .Soma(Saida[0]), .Cout(somador_1_cout));
  SOMADOR somador_2 (.A(A[1]), .B(B[1]), .Cin(somador_1_cout), .Soma(Saida[1]), .Cout(somador_2_cout));
  SOMADOR somador_3 (.A(A[2]), .B(B[2]), .Cin(somador_2_cout), .Soma(Saida[2]), .Cout(somador_3_cout));
  SOMADOR somador_4 (.A(A[3]), .B(B[3]), .Cin(somador_3_cout), .Soma(Saida[3]), .Cout(somador_4_cout));
  SOMADOR somador_5 (.A(A[4]), .B(B[4]), .Cin(somador_4_cout), .Soma(Saida[4]), .Cout(somador_5_cout));
  SOMADOR somador_6 (.A(A[5]), .B(B[5]), .Cin(somador_5_cout), .Soma(Saida[5]), .Cout(somador_6_cout));
  SOMADOR somador_7 (.A(A[6]), .B(B[6]), .Cin(somador_6_cout), .Soma(Saida[6]), .Cout(somador_7_cout));
  SOMADOR somador_8 (.A(A[7]), .B(B[7]), .Cin(somador_7_cout), .Soma(Saida[7]), .Cout(Cout));
endmodule

module SUBTRATOR (
  input  A,
  input  B,
  input  Bin,
  output S,
  output Bout
);

  wire and_1_out, and_2_out, not_1_out, not_2_out, xor_1bit_1_s;

  XOR_1BIT xor_1bit_1 (.A(A), .B(B), .S(xor_1bit_1_s));
  not not_1 (not_1_out, A);
  XOR_1BIT xor_1bit_2 (.A(xor_1bit_1_s), .B(Bin), .S(S));
  not not_2 (not_2_out, xor_1bit_1_s);
  and and_1 (and_1_out, not_2_out, Bin);
  and and_2 (and_2_out, not_1_out, B);
  or or_1 (Bout, and_1_out, and_2_out);
endmodule

module SUBTRATOR_8BITS (
  input  Bin,
  input  [7:0] A,
  input  [7:0] B,
  output [7:0] Saida,
  output Bout
);

  wire subtrator_1_bout, subtrator_2_bout, subtrator_3_bout, subtrator_4_bout, subtrator_5_bout,
       subtrator_6_bout, subtrator_7_bout;

  SUBTRATOR subtrator_1 (.A(A[0]), .B(B[0]), .Bin(Bin), .S(Saida[0]), .Bout(subtrator_1_bout));
  SUBTRATOR subtrator_2 (.A(A[1]), .B(B[1]), .Bin(subtrator_1_bout), .S(Saida[1]), .Bout(subtrator_2_bout));
  SUBTRATOR subtrator_3 (.A(A[2]), .B(B[2]), .Bin(subtrator_2_bout), .S(Saida[2]), .Bout(subtrator_3_bout));
  SUBTRATOR subtrator_4 (.A(A[3]), .B(B[3]), .Bin(subtrator_3_bout), .S(Saida[3]), .Bout(subtrator_4_bout));
  SUBTRATOR subtrator_5 (.A(A[4]), .B(B[4]), .Bin(subtrator_4_bout), .S(Saida[4]), .Bout(subtrator_5_bout));
  SUBTRATOR subtrator_6 (.A(A[5]), .B(B[5]), .Bin(subtrator_5_bout), .S(Saida[5]), .Bout(subtrator_6_bout));
  SUBTRATOR subtrator_7 (.A(A[6]), .B(B[6]), .Bin(subtrator_6_bout), .S(Saida[6]), .Bout(subtrator_7_bout));
  SUBTRATOR subtrator_8 (.A(A[7]), .B(B[7]), .Bin(subtrator_7_bout), .S(Saida[7]), .Bout(Bout));
endmodule

module DESLOCADOR_1BIT_DIR (
  input  [7:0] in_1,
  output [7:0] out_2
);

  wire and_1_out, and_3_out, and_4_out, and_5_out, and_6_out, and_7_out, and_8_out, and_9_out, and_10_out,
       and_11_out, and_12_out, and_14_out, not_1_out;

  not not_1 (not_1_out, 1'b0);
  and and_1 (and_1_out, in_1[0], 1'b0);
  and and_2 (out_2[0], not_1_out, in_1[1]);
  and and_3 (and_3_out, in_1[1], 1'b0);
  or or_1 (out_2[1], and_1_out, and_4_out);
  and and_4 (and_4_out, not_1_out, in_1[2]);
  or or_2 (out_2[2], and_3_out, and_6_out);
  and and_5 (and_5_out, in_1[2], 1'b0);
  and and_6 (and_6_out, not_1_out, in_1[3]);
  and and_7 (and_7_out, in_1[3], 1'b0);
  or or_3 (out_2[3], and_5_out, and_9_out);
  and and_8 (and_8_out, in_1[4], 1'b0);
  and and_9 (and_9_out, not_1_out, in_1[4]);
  or or_4 (out_2[4], and_7_out, and_11_out);
  and and_10 (and_10_out, in_1[5], 1'b0);
  and and_11 (and_11_out, not_1_out, in_1[5]);
  or or_5 (out_2[5], and_8_out, and_12_out);
  and and_12 (and_12_out, not_1_out, in_1[6]);
  or or_6 (out_2[6], and_10_out, and_14_out);
  and and_13 (out_2[7], in_1[6], 1'b0);
  and and_14 (and_14_out, not_1_out, in_1[7]);
endmodule

module DESLOCADOR_2BITS_DIR (
  input  [7:0] In,
  output [7:0] Out
);

  wire [7:0] deslocador_1bit_dir_1_out_2;

  DESLOCADOR_1BIT_DIR deslocador_1bit_dir_1 (.in_1(In), .out_2(deslocador_1bit_dir_1_out_2));
  DESLOCADOR_1BIT_DIR deslocador_1bit_dir_2 (.in_1(deslocador_1bit_dir_1_out_2), .out_2(Out));
endmodule

module DESLOCADOR_1BIT_ESQ (
  input  [7:0] in_1,
  output [7:0] out_2
);

  wire and_2_out, and_3_out, and_4_out, and_5_out, and_6_out, and_7_out, and_8_out, and_9_out, and_10_out,
       and_11_out, and_13_out, and_14_out, not_1_out;

  not not_1 (not_1_out, 1'b1);
  and and_1 (out_2[0], not_1_out, in_1[1]);
  and and_2 (and_2_out, in_1[0], 1'b1);
  and and_3 (and_3_out, in_1[1], 1'b1);
  or or_1 (out_2[1], and_2_out, and_4_out);
  and and_4 (and_4_out, not_1_out, in_1[2]);
  and and_5 (and_5_out, in_1[2], 1'b1);
  or or_2 (out_2[2], and_3_out, and_7_out);
  and and_6 (and_6_out, in_1[3], 1'b1);
  and and_7 (and_7_out, not_1_out, in_1[3]);
  or or_3 (out_2[3], and_5_out, and_8_out);
  and and_8 (and_8_out, not_1_out, in_1[4]);
  or or_4 (out_2[4], and_6_out, and_9_out);
  and and_9 (and_9_out, not_1_out, in_1[5]);
  and and_10 (and_10_out, in_1[4], 1'b1);
  and and_11 (and_11_out, in_1[5], 1'b1);
  or or_5 (out_2[5], and_10_out, and_13_out);
  and and_12 (out_2[7], in_1[6], 1'b1);
  and and_13 (and_13_out, not_1_out, in_1[6]);
  or or_6 (out_2[6], and_11_out, and_14_out);
  and and_14 (and_14_out, not_1_out, in_1[7]);
endmodule

module DESLOCADOR_2BITS_ESQ (
  input  [7:0] in_1,
  output [7:0] out_2
);

  wire [7:0] deslocador_1bit_esq_1_out_2;

  DESLOCADOR_1BIT_ESQ deslocador_1bit_esq_1 (.in_1(in_1), .out_2(deslocador_1bit_esq_1_out_2));
  DESLOCADOR_1BIT_ESQ deslocador_1bit_esq_2 (.in_1(deslocador_1bit_esq_1_out_2), .out_2(out_2));
endmodule

module MUX_2x1 (
  input  A0,
  input  A1,
  input  Select,
  output Y
);

  wire and_1_out, and_2_out, not_1_out;

  not not_1 (not_1_out, Select);
  and and_1 (and_1_out, A0, not_1_out);
  and and_2 (and_2_out, A1, Select);
  or or_1 (Y, and_1_out, and_2_out);
endmodule

module MUX_2X1_8BITS (
  input  [7:0] A1,
  input  [7:0] A0,
  input  in_3,
  output [7:0] Saida
);

  MUX_2x1 mux_2x1_1 (.A0(A0[7]), .A1(A1[7]), .Select(in_3), .Y(Saida[7]));
  MUX_2x1 mux_2x1_2 (.A0(A0[6]), .A1(A1[6]), .Select(in_3), .Y(Saida[6]));
  MUX_2x1 mux_2x1_3 (.A0(A0[5]), .A1(A1[5]), .Select(in_3), .Y(Saida[5]));
  MUX_2x1 mux_2x1_4 (.A0(A0[4]), .A1(A1[4]), .Select(in_3), .Y(Saida[4]));
  MUX_2x1 mux_2x1_5 (.A0(A0[3]), .A1(A1[3]), .Select(in_3), .Y(Saida[3]));
  MUX_2x1 mux_2x1_6 (.A0(A0[2]), .A1(A1[2]), .Select(in_3), .Y(Saida[2]));
  MUX_2x1 mux_2x1_7 (.A0(A0[1]), .A1(A1[1]), .Select(in_3), .Y(Saida[1]));
  MUX_2x1 mux_2x1_8 (.A0(A0[0]), .A1(A1[0]), .Select(in_3), .Y(Saida[0]));
endmodule

module MUX_4X1_8bBITS (
  input  [7:0] A0,
  input  [7:0] A1,
  input  [7:0] A2,
  input  [7:0] A3,
  input  [1:0] in_5,
  output [7:0] Saida
);

  wire [7:0] mux_2x1_8bits_1_saida, mux_2x1_8bits_2_saida;

  MUX_2X1_8BITS mux_2x1_8bits_1 (.Saida(mux_2x1_8bits_1_saida), .A1(A1), .A0(A0), .in_3(in_5[0]));
  MUX_2X1_8BITS mux_2x1_8bits_2 (.Saida(mux_2x1_8bits_2_saida), .A1(A3), .A0(A2), .in_3(in_5[0]));
  MUX_2X1_8BITS mux_2x1_8bits_3 (.Saida(Saida), .A1(mux_2x1_8bits_2_saida), .A0(mux_2x1_8bits_1_saida), .in_3(in_5[1]));
endmodule

module MUX_8X1_8BITS (
  input  [7:0] A0,
  input  [7:0] A1,
  input  [7:0] A2,
  input  [7:0] A3,
  input  [7:0] A4,
  input  [7:0] A5,
  input  [7:0] A6,
  input  [7:0] A7,
  input  [2:0] Select,
  output [7:0] Saida
);

  wire [7:0] mux_4x1_8bbits_1_saida, mux_4x1_8bbits_2_saida;

  MUX_4X1_8bBITS mux_4x1_8bbits_1 (
    .A0(A0), .A1(A1), .A2(A2), .A3(A3), .in_5(Select[1:0]), .Saida(mux_4x1_8bbits_1_saida));
  MUX_4X1_8bBITS mux_4x1_8bbits_2 (
    .A0(A4), .A1(A5), .A2(A6), .A3(A7), .in_5(Select[1:0]), .Saida(mux_4x1_8bbits_2_saida));
  MUX_2X1_8BITS mux_2x1_8bits_1 (
    .Saida(Saida), .A1(mux_4x1_8bbits_2_saida), .A0(mux_4x1_8bbits_1_saida), .in_3(Select[2]));
endmodule

module MUX_16X1_8BITS (
  input  [7:0] in_1,
  input  [7:0] in_2,
  input  [7:0] in_3,
  input  [7:0] in_4,
  input  [7:0] in_5,
  input  [7:0] in_6,
  input  [7:0] in_7,
  input  [7:0] in_8,
  input  [7:0] in_9,
  input  [7:0] in_10,
  input  [3:0] in_11,
  output [7:0] out_12
);

  wire [7:0] mux_8x1_8bits_1_saida, mux_8x1_8bits_2_saida;

  MUX_8X1_8BITS mux_8x1_8bits_1 (
    .A0(in_1), .A1(in_2), .A2(in_3), .A3(in_4), .A4(in_5), .A5(in_6), .A6(in_7), .A7(in_8),
    .Select(in_11[2:0]), .Saida(mux_8x1_8bits_1_saida));
  MUX_8X1_8BITS mux_8x1_8bits_2 (
    .A0(in_9), .A1(in_10), .A3({8{1'b0}}), .A4({8{1'b0}}), .A5({8{1'b0}}), .A6({8{1'b0}}), .A7({8{1'b0}}),
    .Select(in_11[2:0]), .Saida(mux_8x1_8bits_2_saida));  // open: A2
  MUX_2X1_8BITS mux_2x1_8bits_1 (
    .Saida(out_12), .A1(mux_8x1_8bits_2_saida), .A0(mux_8x1_8bits_1_saida), .in_3(in_11[3]));
endmodule
