// Logisim project 11-EXTENSOR_4_PARA_8_BITS.circ as structural Verilog: 1 circuit, main circuit Extensor de sinal 4 bits para 8 bits
module Extensor_de_sinal_4_bits_para_8_bits (
  input  [3:0] Entrada,
  output [7:0] \Saída 
);


  assign \Saída  = {4'b0000, Entrada};

  // Notes on the sheet:
  //   Extensor de sinal de 4 bits para 8 bits
endmodule
