// Logisim project 12-MAQUINA_DE_ESTADOS.circ as structural Verilog: 4 circuits, main circuit MAQUINA_DE_ESTADOS
module MAQUINA_DE_ESTADOS (
  input  X,
  input  Preset,
  input  Clear,
  output Y
);

  wire and_1_out, and_2_out, and_3_out, and_4_out, and_5_out, and_6_out, and_7_out, and_8_out, and_9_out,
       and_10_out, and_11_out, and_12_out, clock_1_out, decoder_3x8_1_out_4, decoder_3x8_1_out_5,
       decoder_3x8_1_out_6, decoder_3x8_1_out_7, decoder_3x8_1_out_8, decoder_3x8_1_out_9,
       decoder_3x8_1_out_10, ff_d_1_out_5, ff_d_2_out_5, ff_d_3_out_5, not_1_out, not_2_out, not_3_out,
       not_4_out, not_5_out, not_6_out, not_7_out, not_8_out, not_9_out, not_10_out, not_11_out, not_12_out,
       not_13_out, not_14_out, not_15_out, not_16_out, or_1_out, or_2_out, or_3_out;

  DECODER_3X8 decoder_3x8_1 (
    .S0(ff_d_3_out_5), .S1(ff_d_2_out_5), .S2(ff_d_1_out_5), .out_4(decoder_3x8_1_out_4),
    .out_5(decoder_3x8_1_out_5), .out_6(decoder_3x8_1_out_6), .out_7(decoder_3x8_1_out_7),
    .out_8(decoder_3x8_1_out_8), .out_9(decoder_3x8_1_out_9), .out_10(decoder_3x8_1_out_10));  // open: out_11
  not not_1 (not_1_out, ff_d_2_out_5);
  and and_1 (and_1_out, ff_d_1_out_5, not_1_out);
  Clock clock_1 (.out(clock_1_out));
  LED A (.in(decoder_3x8_1_out_4));
  not not_2 (not_2_out, ff_d_3_out_5);
  not not_3 (not_3_out, ff_d_1_out_5);
  and and_2 (and_2_out, not_3_out, ff_d_2_out_5, ff_d_3_out_5);
  and and_3 (and_3_out, ff_d_1_out_5, not_2_out, X);
  or or_1 (or_1_out, and_1_out, and_2_out, and_3_out);
  LED B (.in(decoder_3x8_1_out_5));
  LED C (.in(decoder_3x8_1_out_6));
  LED D (.in(decoder_3x8_1_out_7));
  FF_D ff_d_1 (.D(or_1_out), .CLK(clock_1_out), .out_5(ff_d_1_out_5), .Preset(Preset), .Clear(Clear));  // open: out_6
  LED F (.in(decoder_3x8_1_out_9));
  LED E (.in(decoder_3x8_1_out_8));
  not not_4 (not_4_out, ff_d_1_out_5);
  not not_5 (not_5_out, ff_d_2_out_5);
  and and_4 (and_4_out, not_5_out, ff_d_3_out_5);
  LED G (.in(decoder_3x8_1_out_10));
  not not_6 (not_6_out, ff_d_3_out_5);
  not not_7 (not_7_out, ff_d_3_out_5);
  and and_5 (and_5_out, not_4_out, ff_d_2_out_5, not_6_out);
  and and_6 (and_6_out, ff_d_2_out_5, not_7_out, X);
  or or_2 (or_2_out, and_4_out, and_5_out, and_6_out);
  FF_D ff_d_2 (.D(or_2_out), .CLK(clock_1_out), .out_5(ff_d_2_out_5), .Preset(Preset), .Clear(Clear));  // open: out_6
  not not_8 (not_8_out, ff_d_3_out_5);
  not not_9 (not_9_out, ff_d_1_out_5);
  not not_10 (not_10_out, ff_d_2_out_5);
  and and_7 (and_7_out, ff_d_1_out_5, not_10_out, not_8_out);
  and and_8 (and_8_out, not_9_out, ff_d_2_out_5, not_11_out);
  or or_3 (or_3_out, and_7_out, and_8_out, and_9_out);
  not not_11 (not_11_out, ff_d_3_out_5);
  not not_12 (not_12_out, ff_d_3_out_5);
  not not_13 (not_13_out, ff_d_1_out_5);
  and and_9 (and_9_out, not_13_out, not_12_out, X);
  FF_D ff_d_3 (.D(or_3_out), .CLK(clock_1_out), .out_5(ff_d_3_out_5), .Preset(Preset), .Clear(Clear));  // open: out_6
  not not_14 (not_14_out, ff_d_1_out_5);
  not not_15 (not_15_out, ff_d_2_out_5);
  not not_16 (not_16_out, ff_d_1_out_5);
  and and_10 (and_10_out, ff_d_1_out_5, not_15_out);
  and and_11 (and_11_out, not_14_out, ff_d_2_out_5);
  or or_4 (Y, and_10_out, and_11_out, and_12_out);
  and and_12 (and_12_out, not_16_out, ff_d_3_out_5);

  // Notes on the sheet:
  //   Estados:
  //   Essa é uma máquina de estados que descreve o seguinte projeto:
  //   Depois desses cinco pulsos de clock, Y deve voltar a ser 0, mesmo que X ainda seja 1.
  //   Pois a condição para Y ser igual a 1 é a troca de estado de X de 0 para 1.
  //   Dada uma entrada X e uma saída Y, quando X passar de 0 para 1, Y deve ser 1 por 5 pulsos de clock. 
  //   Maquina de Estados
endmodule

module FF_JK (
  input  Preset,
  input  J,
  input  Clock,
  input  K,
  input  Clear,
  output Q,
  output nQ
);

  wire nand_1_out, nand_2_out, nand_3_out, nand_4_out, nand_5_out, nand_6_out, not_1_out, not_2_out,
       not_3_out;

  not not_1 (not_1_out, Preset);
  nand nand_1 (nand_1_out, nQ, J, Clock);
  not not_2 (not_2_out, Clock);
  nand nand_2 (nand_2_out, Clock, K, Q);
  not not_3 (not_3_out, Clear);
  nand nand_3 (nand_3_out, not_1_out, nand_1_out, nand_4_out);
  nand nand_4 (nand_4_out, nand_3_out, nand_2_out, not_3_out);
  nand nand_5 (nand_5_out, not_3_out, nand_3_out, not_2_out);
  nand nand_6 (nand_6_out, not_2_out, nand_4_out, not_1_out);
  nand nand_7 (Q, not_1_out, nand_5_out, nQ);
  nand nand_8 (nQ, Q, nand_6_out, not_3_out);
endmodule

module FF_D (
  input  D,
  input  CLK,
  input  Preset,
  input  Clear,
  output out_5,
  output out_6
);

  wire not_1_out;

  not not_1 (not_1_out, D);
  FF_JK ff_jk_1 (.Preset(Preset), .J(D), .Clock(CLK), .K(not_1_out), .Clear(Clear), .Q(out_5), .nQ(out_6));
endmodule

module DECODER_3X8 (
  input  S0,
  input  S1,
  input  S2,
  output out_4,
  output out_5,
  output out_6,
  output out_7,
  output out_8,
  output out_9,
  output out_10,
  output out_11
);

  wire not_1_out, not_2_out, not_3_out, not_4_out, not_5_out, not_6_out, not_7_out, not_8_out, not_9_out,
       not_10_out, not_11_out, not_12_out;

  not not_1 (not_1_out, S0);
  not not_2 (not_2_out, S1);
  not not_3 (not_3_out, S2);
  not not_4 (not_4_out, S1);
  not not_5 (not_5_out, S2);
  not not_6 (not_6_out, S0);
  not not_7 (not_7_out, S2);
  not not_8 (not_8_out, S2);
  not not_9 (not_9_out, S0);
  not not_10 (not_10_out, S1);
  not not_11 (not_11_out, S1);
  not not_12 (not_12_out, S0);
  and and_1 (out_4, not_1_out, not_2_out, not_3_out);
  and and_2 (out_5, S0, not_4_out, not_5_out);
  and and_3 (out_6, not_6_out, S1, not_7_out);
  and and_4 (out_7, S0, S1, not_8_out);
  and and_5 (out_8, not_9_out, not_10_out, S2);
  and and_6 (out_9, S0, not_11_out, S2);
  and and_7 (out_10, not_12_out, S1, S2);
  and and_8 (out_11, S0, S1, S2);
endmodule
