// Logisim project 13-CONTADOR_SINCRONO.circ as structural Verilog: 3 circuits, main circuit CONTADOR_SINCRONO_DEC
module CONTADOR_SINCRONO_DEC (
  input  Preset,
  input  Clear,
  output out_3,
  output out_4,
  output out_5,
  output out_6
);

  wire and_1_out, and_2_out, and_3_out, clock_1_out, ff_t_1_nq, ff_t_3_nq, ff_t_4_nq, not_1_out, or_1_out;

  Clock clock_1 (.out(clock_1_out));
  or or_1 (or_1_out, Clear, and_3_out);
  FF_T ff_t_1 (.CLK(clock_1_out), .Preset(Preset), .Clear(or_1_out), .Q(out_3), .nQ(ff_t_1_nq), .T(1'b1));
  FF_T ff_t_2 (.CLK(clock_1_out), .Preset(Preset), .Clear(or_1_out), .Q(out_4), .T(out_3));  // open: nQ
  and and_1 (and_1_out, out_3, out_4);
  and and_2 (and_2_out, and_1_out, out_5);
  FF_T ff_t_3 (.CLK(clock_1_out), .Preset(Preset), .Clear(or_1_out), .Q(out_5), .nQ(ff_t_3_nq), .T(and_1_out));
  FF_T ff_t_4 (.CLK(clock_1_out), .Preset(Preset), .Clear(or_1_out), .Q(out_6), .nQ(ff_t_4_nq), .T(and_2_out));
  not not_1 (not_1_out, ff_t_4_nq);
  and and_3 (and_3_out, not_1_out, ff_t_3_nq, out_4, ff_t_1_nq);

  // Notes on the sheet:
  //   Contador Sincrono Decada
  //   Ligar preset ativa a condição de reinicio da clock, ativando tbm o clear, gerando a saida invalida 1 e 1 em Q e ~Q.
  //   Porta AND ativa os clears dos flip-flops, quando atigir o número 10, ou 1010
endmodule

module FF_JK (
  input  Preset,
  input  J,
  input  CLK,
  input  K,
  input  Clear,
  output Q,
  output nQ
);

  wire nand_1_out, nand_2_out, nand_3_out, nand_4_out, nand_5_out, nand_6_out, not_1_out, not_2_out,
       not_3_out;

  not not_1 (not_1_out, Preset);
  nand nand_1 (nand_1_out, nQ, J, CLK);
  nand nand_2 (nand_2_out, CLK, K, Q);
  not not_2 (not_2_out, Clear);
  not not_3 (not_3_out, CLK);
  nand nand_3 (nand_3_out, not_1_out, nand_1_out, nand_4_out);
  nand nand_4 (nand_4_out, nand_3_out, nand_2_out, not_2_out);
  nand nand_5 (nand_5_out, not_2_out, nand_3_out, not_3_out);
  nand nand_6 (nand_6_out, not_3_out, nand_4_out, not_1_out);
  nand nand_7 (Q, not_1_out, nand_5_out, nQ);
  nand nand_8 (nQ, Q, nand_6_out, not_2_out);
endmodule

module FF_T (
  input  T,
  input  CLK,
  input  Preset,
  input  Clear,
  output Q,
  output nQ
);

  FF_JK ff_jk_1 (.Preset(Preset), .J(T), .CLK(CLK), .K(T), .Clear(Clear), .Q(Q), .nQ(nQ));
endmodule
