// Logisim project 14-DETECTOR_PARIDADE_IMPAR.circ as structural Verilog: 3 circuits, main circuit DETECTOR_PARIDADE_8_ENTRAD
module DETECTOR_PARIDADE_8_ENTRAD (
  input  in_1,
  input  in_2,
  input  in_3,
  input  in_4,
  input  in_5,
  input  in_6,
  input  in_7,
  input  in_8,
  output out_9
);

  wire detector_paridade_4_entrad_1_out_5, detector_paridade_4_entrad_2_out_5;

  DETECTOR_PARIDADE_4_ENTRAD detector_paridade_4_entrad_1 (
    .A(in_1), .B(in_2), .C(in_3), .D(in_4), .out_5(detector_paridade_4_entrad_1_out_5));
  DETECTOR_PARIDADE_4_ENTRAD detector_paridade_4_entrad_2 (
    .A(in_5), .B(in_6), .C(in_7), .D(in_8), .out_5(detector_paridade_4_entrad_2_out_5));
  GATE_XOR gate_xor_1 (
    .in_1(detector_paridade_4_entrad_1_out_5), .in_2(detector_paridade_4_entrad_2_out_5), .out_3(out_9));

  // Notes on the sheet:
  //   Detector de Paridade Impar com 8 entradas
  //   Um dector de paridade impar de 2 entradas é apenas o XOR entre estas 2 entradas.
  //   Para colocar mais entradas, basta colocar mais um XOR para essa nova entrada e o resultado do XOR anterior.
endmodule

module GATE_XOR (
  input  in_1,
  input  in_2,
  output out_3
);

  wire and_1_out, and_2_out, not_1_out, not_2_out;

  not not_1 (not_1_out, in_2);
  not not_2 (not_2_out, in_1);
  and and_1 (and_1_out, in_1, not_1_out);
  and and_2 (and_2_out, not_2_out, in_2);
  or or_1 (out_3, and_1_out, and_2_out);
endmodule

module DETECTOR_PARIDADE_4_ENTRAD (
  input  A,
  input  B,
  input  C,
  input  D,
  output out_5
);

  wire gate_xor_1_out_3, gate_xor_2_out_3;

  GATE_XOR gate_xor_1 (.in_1(A), .in_2(B), .out_3(gate_xor_1_out_3));
  GATE_XOR gate_xor_2 (.in_1(gate_xor_1_out_3), .in_2(C), .out_3(gate_xor_2_out_3));
  GATE_XOR gate_xor_3 (.in_1(gate_xor_2_out_3), .in_2(D), .out_3(out_5));
endmodule
