// Logisim project 15-CIRCUITO_OTIMIZADO_COM_MAPA_DE_KARNAUGH.circ as structural Verilog: 1 circuit, main circuit Otimização lógica
module \Otimização_lógica  (
  input  [2:0] A_B_C,
  input  [2:0] A_B_C_2,
  output S,
  output S_2
);

  wire A_prime_BC_out, AB_out, AB_prime_C_out, ABC_out, ABC_prime_out, AC_out, BC_out;

  and A_prime_BC (A_prime_BC_out, ~A_B_C[2], A_B_C[1], A_B_C[0]);  // AND_Gate
  and AB_prime_C (AB_prime_C_out, A_B_C[2], ~A_B_C[1], A_B_C[0]);  // AND_Gate
  and ABC_prime (ABC_prime_out, A_B_C[2], A_B_C[1], ~A_B_C[0]);  // AND_Gate
  and ABC (ABC_out, A_B_C[2], A_B_C[1], A_B_C[0]);
  and AC (AC_out, A_B_C_2[2], A_B_C_2[0]);
  and AB (AB_out, A_B_C_2[2], A_B_C_2[1]);
  and BC (BC_out, A_B_C_2[1], A_B_C_2[0]);
  or or_1 (S, A_prime_BC_out, AB_prime_C_out, ABC_prime_out, ABC_out);
  or or_2 (S_2, AC_out, AB_out, BC_out);

  // Notes on the sheet:
  //   Sem otimização:
  //   Com otimização:
  //   A | B | C | S
  //   0 | 0 | 0 | 0
  //   0 | 0 | 1 | 0
  //   0 | 1 | 0 | 0
  //   0 | 1 | 1 | 1
  //   1 | 0 | 0 | 0
  //   1 | 0 | 1 | 1
  //   1 | 1 | 0 | 1
  //   1 | 1 | 1 | 1
  //   Resolva um problema de otimização lógica utilizando mapas de Karnaugh e implemente o circuito otimizado.
  //   S = A'BC + AB'C + ABC' + ABC
  //   S = AC + AB + BC
endmodule
