// Logisim project 16-DECODIFICADOR_DE_7_SEGMENTOS_FORM_HEX.circ as structural Verilog: 1 circuit, main circuit Decodificador de 7 Segmentos Hexadecimal
module Decodificador_de_7_Segmentos_Hexadecimal (
  input  A,
  input  B,
  input  C,
  input  D
);

  wire _0_out, _1_out, _2_out, _3_out, _4_out, _5_out, _6_out, _7_out, _8_out, _9_out, A_2_out, A_out,
       B_2_out, B_out, C_2_out, C_out, D_2_out, D_out, E_2_out, E_out, F_2_out, F_out, G_out;

  and _0 (_0_out, ~A, ~B, ~C, ~D);  // AND_Gate
  and _1 (_1_out, ~A, ~B, ~C, D);  // AND_Gate
  and _2 (_2_out, ~A, ~B, C, ~D);  // AND_Gate
  and _3 (_3_out, ~A, ~B, C, D);  // AND_Gate
  and _4 (_4_out, ~A, B, ~C, ~D);  // AND_Gate
  and _5 (_5_out, ~A, B, ~C, D);  // AND_Gate
  and _6 (_6_out, ~A, B, C, ~D);  // AND_Gate
  and _8 (_8_out, A, ~B, ~C, ~D);  // AND_Gate
  and _7 (_7_out, ~A, B, C, D);  // AND_Gate
  and _9 (_9_out, A, ~B, ~C, D);  // AND_Gate
  and u_A (A_out, A, ~B, C, ~D);  // AND_Gate
  and u_B (B_out, A, ~B, C, D);  // AND_Gate
  and u_C (C_out, A, B, ~C, ~D);  // AND_Gate
  and u_D (D_out, A, B, ~C, D);  // AND_Gate
  and E (E_out, A, B, C, ~D);  // AND_Gate
  and F (F_out, A, B, C, D);
  or A_2 (A_2_out, _0_out, _2_out, _3_out, _5_out, _6_out, _7_out, _8_out, _9_out, A_out, C_out, E_out, F_out);
  or B_2 (B_2_out, _0_out, _1_out, _2_out, _3_out, _4_out, _7_out, _8_out, _9_out, A_out, D_out);
  or C_2 (C_2_out, _0_out, _1_out, _3_out, _4_out, _5_out, _6_out, _7_out, _8_out, _9_out, A_out, B_out, D_out);
  or D_2 (D_2_out, _0_out, _2_out, _3_out, _5_out, _6_out, _8_out, _9_out, B_out, C_out, D_out, E_out);
  or E_2 (E_2_out, _0_out, _2_out, _6_out, _8_out, A_out, B_out, C_out, D_out, E_out, F_out);
  or F_2 (F_2_out, F_out, _0_out, _4_out, _5_out, _6_out, _8_out, _9_out, A_out, B_out, C_out, E_out);
  or G (G_out, _2_out, _3_out, _4_out, _5_out, _6_out, _8_out, _9_out, A_out, B_out, D_out, E_out, F_out);
  _7_Segment_Display u_7_segment_display_1 (
    .g(G_out), .f(F_2_out), .a(A_2_out), .b(B_2_out), .e(E_2_out), .d(D_2_out), .c(C_2_out));  // open: dp

  // Notes on the sheet:
  //   Decodificador de 7 Segmentos: Projete um circuito que converta um número binário de 4 bits para os sinais necessários para acionar um display de 7 segmentos (formato hexadecimal)
  //   Decodificador de Endereços
endmodule
