// Logisim project 17-DETECTOR_NUMERO_PRIMO_COM_MAPA_DE_KARNAUGH.circ as structural Verilog: 1 circuit, main circuit Detector de Número Primo
module \Detector_de_Número_Primo  (
  input  [3:0] A_B_C_D,
  output S
);

  wire A_prime_B_prime_C_out, A_prime_CD_out, B_prime_CD_out, BC_prime_D_out;

  and A_prime_B_prime_C (A_prime_B_prime_C_out, ~A_B_C_D[3], ~A_B_C_D[2], A_B_C_D[1]);  // AND_Gate
  and A_prime_CD (A_prime_CD_out, ~A_B_C_D[3], A_B_C_D[1], A_B_C_D[0]);  // AND_Gate
  and BC_prime_D (BC_prime_D_out, A_B_C_D[2], ~A_B_C_D[1], A_B_C_D[0]);  // AND_Gate
  and B_prime_CD (B_prime_CD_out, ~A_B_C_D[2], A_B_C_D[1], A_B_C_D[0]);  // AND_Gate
  or or_1 (S, A_prime_B_prime_C_out, A_prime_CD_out, BC_prime_D_out, B_prime_CD_out);

  // Notes on the sheet:
  //   3 2 1 0
  //   Detector de Número Primo
  //   Fórmula simplificada -> S = A'B'C + A'CD + BC'D + B'CD
  //   Fórmula sem simplificação -> S = A'B'CD' + A'B'CD + A'BC'D + A'BCD + AB'CD + ABC'D
  //   Saída = 1, Número é primo
  //   Saída = 0, Número não é primo
endmodule
