// Logisim project 2-MUX_4_X_1.circ as structural Verilog
module Multiplexador_de_4_entradas (
  input  I3,
  input  I2,
  input  I1,
  input  I0,
  input  S0,
  input  S1,
  output S
);

  wire and_1_out, and_2_out, and_3_out, and_4_out, not_1_out, not_2_out;

  not not_1 (not_1_out, S0);
  not not_2 (not_2_out, S1);
  and and_1 (and_1_out, I3, S0, S1);
  and and_2 (and_2_out, I2, not_1_out, S1);
  and and_3 (and_3_out, I1, not_2_out, S0);
  and and_4 (and_4_out, I0, not_1_out, not_2_out);
  or or_1 (S, and_1_out, and_2_out, and_3_out, and_4_out);

  // Notes on the sheet:
  //   Multiplexador 4x1
endmodule
