// Logisim project 3-XOR.circ as structural Verilog: 1 circuit, main circuit Porta lógica XOR
module \Porta_lógica_XOR  (
  input  A,
  input  B,
  output S
);

  wire and_1_out, and_2_out, not_1_out, not_2_out;

  not not_1 (not_1_out, A);
  not not_2 (not_2_out, B);
  and and_1 (and_1_out, not_1_out, B);
  and and_2 (and_2_out, A, not_2_out);
  or or_1 (S, and_1_out, and_2_out);

  // Notes on the sheet:
  //   Porta XOR
endmodule
