// Logisim project 4-SOMADOR_8_BITS_MAIS_4.circ as structural Verilog: 3 circuits, main circuit Somador de 8 bits
module Somador_de_8_bits (
  input  [7:0] A,
  output [7:0] SOMA,
  output out_3
);

  wire somador_de_1_bit_1_cout, somador_de_1_bit_2_cout, somador_de_1_bit_3_cout, somador_de_1_bit_4_cout,
       somador_de_1_bit_5_cout, somador_de_1_bit_6_cout, somador_de_1_bit_7_cout;

  Somador_de_1_bit somador_de_1_bit_1 (.A0(A[0]), .A1(1'b0), .cin(1'b0), .S(SOMA[0]), .cout(somador_de_1_bit_1_cout));
  Somador_de_1_bit somador_de_1_bit_2 (
    .A0(A[1]), .A1(1'b0), .cin(somador_de_1_bit_1_cout), .S(SOMA[1]), .cout(somador_de_1_bit_2_cout));
  Somador_de_1_bit somador_de_1_bit_3 (
    .A0(A[2]), .A1(1'b1), .cin(somador_de_1_bit_2_cout), .S(SOMA[2]), .cout(somador_de_1_bit_3_cout));
  Somador_de_1_bit somador_de_1_bit_4 (
    .A0(A[3]), .A1(1'b0), .cin(somador_de_1_bit_3_cout), .S(SOMA[3]), .cout(somador_de_1_bit_4_cout));
  Somador_de_1_bit somador_de_1_bit_5 (
    .A0(A[4]), .A1(1'b0), .cin(somador_de_1_bit_4_cout), .S(SOMA[4]), .cout(somador_de_1_bit_5_cout));
  Somador_de_1_bit somador_de_1_bit_6 (
    .A0(A[5]), .A1(1'b0), .cin(somador_de_1_bit_5_cout), .S(SOMA[5]), .cout(somador_de_1_bit_6_cout));
  Somador_de_1_bit somador_de_1_bit_7 (
    .A0(A[6]), .A1(1'b0), .cin(somador_de_1_bit_6_cout), .S(SOMA[6]), .cout(somador_de_1_bit_7_cout));
  Somador_de_1_bit somador_de_1_bit_8 (.A0(A[7]), .A1(1'b0), .cin(somador_de_1_bit_7_cout), .S(SOMA[7]), .cout(out_3));

  // Notes on the sheet:
  //   Valor 4 em binário
  //   Somador de 8 bits que recebe um valor inteiro e soma com o valor 4
endmodule

module Somador_de_1_bit (
  input  A0,
  input  A1,
  input  cin,
  output S,
  output cout
);

  wire and_1_out, and_2_out, and_3_out, xor_1_s;

  XOR xor_1 (.A(A1), .B(A0), .S(xor_1_s));
  and and_1 (and_1_out, A0, A1);
  and and_2 (and_2_out, A0, cin);
  and and_3 (and_3_out, A1, cin);
  XOR xor_2 (.A(cin), .B(xor_1_s), .S(S));
  or or_1 (cout, and_1_out, and_2_out, and_3_out);
endmodule

module XOR (
  input  A,
  input  B,
  output S
);

  wire and_1_out, and_2_out, not_1_out, not_2_out;

  not not_1 (not_1_out, A);
  not not_2 (not_2_out, B);
  and and_1 (and_1_out, not_1_out, B);
  and and_2 (and_2_out, A, not_2_out);
  or or_1 (S, and_1_out, and_2_out);

  // Notes on the sheet:
  //   Porta XOR
endmodule
