// Logisim project 5-MEM_ROM_8X8.circ as structural Verilog: 5 circuits, main circuit MEMORIA_ROM_8X8
module MEMORIA_ROM_8X8 (
  input  [2:0] \Endereço ,
  input  Enable,
  output [7:0] Saida
);

  MUX_8X1_8BITS mux_8x1_8bits_1 (
    .A0(8'h1), .A1(8'h2), .A2(8'h3), .A3(8'h1f), .A4(8'h10), .A5(8'h11), .A6(8'h12), .A7(8'h14),
    .Select(\Endereço ), .Saida(Saida), .Enable(Enable));

  // Notes on the sheet:
  //   Endereços:
  //   Palavras:
  //   001
  //   000
  //   Memória ROM 8x8
  //   011
  //   100
  //   010
  //   110
  //   101
  //   As oito entradas/constantes do multiplexador são as palavras da ROM, e estão em formato hexadecimal.
  //   111
  //   Esta é uma memória ROM feita com um multiplexador 8x1 de oito bits que atua como um decodificador do endereço informado.
  //   Acessamos as palavras por meio do endereço fornecido ao multiplexador, que faz o papel de seletor no multiplexador.
endmodule

module MUX_2X1 (
  input  A0,
  input  A1,
  input  Select,
  input  Enable,
  output Saida
);

  wire and_1_out, and_2_out, not_1_out, or_1_out;

  not not_1 (not_1_out, Select);
  and and_1 (and_1_out, A0, not_1_out);
  and and_2 (and_2_out, A1, Select);
  or or_1 (or_1_out, and_1_out, and_2_out);
  and and_3 (Saida, or_1_out, Enable);
endmodule

module MUX_2X1_8BITS (
  input  [7:0] A1,
  input  [7:0] A0,
  input  Seletor,
  input  Enable,
  output [7:0] Saida
);

  MUX_2X1 mux_2x1_1 (.A0(A0[7]), .A1(A1[7]), .Select(Seletor), .Saida(Saida[7]), .Enable(Enable));
  MUX_2X1 mux_2x1_2 (.A0(A0[6]), .A1(A1[6]), .Select(Seletor), .Saida(Saida[6]), .Enable(Enable));
  MUX_2X1 mux_2x1_3 (.A0(A0[5]), .A1(A1[5]), .Select(Seletor), .Saida(Saida[5]), .Enable(Enable));
  MUX_2X1 mux_2x1_4 (.A0(A0[4]), .A1(A1[4]), .Select(Seletor), .Saida(Saida[4]), .Enable(Enable));
  MUX_2X1 mux_2x1_5 (.A0(A0[3]), .A1(A1[3]), .Select(Seletor), .Saida(Saida[3]), .Enable(Enable));
  MUX_2X1 mux_2x1_6 (.A0(A0[2]), .A1(A1[2]), .Select(Seletor), .Saida(Saida[2]), .Enable(Enable));
  MUX_2X1 mux_2x1_7 (.A0(A0[1]), .A1(A1[1]), .Select(Seletor), .Saida(Saida[1]), .Enable(Enable));
  MUX_2X1 mux_2x1_8 (.A0(A0[0]), .A1(A1[0]), .Select(Seletor), .Saida(Saida[0]), .Enable(Enable));
endmodule

module MUX_4X1_8BITS (
  input  [7:0] A0,
  input  [7:0] A1,
  input  [7:0] A2,
  input  [7:0] A3,
  input  [1:0] Select,
  input  Enable,
  output [7:0] Saida
);

  wire [7:0] _1_saida, _2_saida;

  MUX_2X1_8BITS _1 (.Seletor(Select[0]), .Saida(_1_saida), .A1(A1), .A0(A0), .Enable(Enable));
  MUX_2X1_8BITS _2 (.Seletor(Select[0]), .Saida(_2_saida), .A1(A3), .A0(A2), .Enable(Enable));
  MUX_2X1_8BITS _3 (.Seletor(Select[1]), .Saida(Saida), .A1(_2_saida), .A0(_1_saida), .Enable(Enable));
endmodule

module MUX_8X1_8BITS (
  input  [7:0] A0,
  input  [7:0] A1,
  input  [7:0] A2,
  input  [7:0] A3,
  input  [7:0] A4,
  input  [7:0] A5,
  input  [7:0] A6,
  input  [7:0] A7,
  input  [2:0] Select,
  input  Enable,
  output [7:0] Saida
);

  wire [7:0] _1_saida, _2_saida;

  MUX_4X1_8BITS _1 (.A0(A0), .A1(A1), .A2(A2), .A3(A3), .Select(Select[1:0]), .Saida(_1_saida), .Enable(Enable));
  MUX_4X1_8BITS _2 (.A0(A4), .A1(A5), .A2(A6), .A3(A7), .Select(Select[1:0]), .Saida(_2_saida), .Enable(Enable));
  MUX_2X1_8BITS _3 (.Seletor(Select[2]), .Saida(Saida), .A1(_2_saida), .A0(_1_saida), .Enable(Enable));
endmodule
