// Logisim project 7-BANCO_DE_REGISTRADORES_8BITS.circ as structural Verilog: 12 circuits, main circuit BANCO_REGISTRADORES_8BITS
module BANCO_REGISTRADORES_8BITS (
  input  Able_Read1,
  input  [3:0] Add_Reg1,
  input  Able_Reg2,
  input  [7:0] Write_Data,
  input  Clear,
  input  [3:0] Add_Reg2,
  input  [3:0] Add_Reg0,
  input  Able_Write,
  output [7:0] Read_Reg1,
  output [7:0] Read_Reg2
);

  wire clock_1_out, demux_16x1_1_s0, demux_16x1_1_s1, demux_16x1_1_s2, demux_16x1_1_s3, demux_16x1_1_s4,
       demux_16x1_1_s5, demux_16x1_1_s6, demux_16x1_1_s7, demux_16x1_1_s8, demux_16x1_1_s9, demux_16x1_1_s10,
       demux_16x1_1_s11, demux_16x1_1_s12, demux_16x1_1_s13, demux_16x1_1_s14, demux_16x1_1_s15;
  wire [7:0] registrador_8bits_1_q, registrador_8bits_2_q, registrador_8bits_3_q, registrador_8bits_4_q,
       registrador_8bits_5_q, registrador_8bits_6_q, registrador_8bits_7_q, registrador_8bits_8_q,
       registrador_8bits_9_q, registrador_8bits_10_q, registrador_8bits_11_q, registrador_8bits_12_q,
       registrador_8bits_13_q, registrador_8bits_14_q, registrador_8bits_15_q, registrador_8bits_16_q;

  Clock clock_1 (.out(clock_1_out));
  DEMUX_16X1 demux_16x1_1 (
    .Data(clock_1_out), .Select(Add_Reg0), .in_3(Able_Write), .S0(demux_16x1_1_s0), .S1(demux_16x1_1_s1),
    .S2(demux_16x1_1_s2), .S3(demux_16x1_1_s3), .S4(demux_16x1_1_s4), .S5(demux_16x1_1_s5),
    .S6(demux_16x1_1_s6), .S7(demux_16x1_1_s7), .S8(demux_16x1_1_s8), .S9(demux_16x1_1_s9),
    .S10(demux_16x1_1_s10), .S11(demux_16x1_1_s11), .S12(demux_16x1_1_s12), .S13(demux_16x1_1_s13),
    .S14(demux_16x1_1_s14), .S15(demux_16x1_1_s15));
  REGISTRADOR_8BITS registrador_8bits_1 (
    .Data(Write_Data), .Clock(demux_16x1_1_s0), .Clear(Clear), .Q(registrador_8bits_1_q));
  REGISTRADOR_8BITS registrador_8bits_2 (
    .Data(Write_Data), .Clock(demux_16x1_1_s1), .Clear(Clear), .Q(registrador_8bits_2_q));
  REGISTRADOR_8BITS registrador_8bits_3 (
    .Data(Write_Data), .Clock(demux_16x1_1_s2), .Clear(Clear), .Q(registrador_8bits_3_q));
  REGISTRADOR_8BITS registrador_8bits_4 (
    .Data(Write_Data), .Clock(demux_16x1_1_s3), .Clear(Clear), .Q(registrador_8bits_4_q));
  REGISTRADOR_8BITS registrador_8bits_5 (
    .Data(Write_Data), .Clock(demux_16x1_1_s4), .Clear(Clear), .Q(registrador_8bits_5_q));
  REGISTRADOR_8BITS registrador_8bits_6 (
    .Data(Write_Data), .Clock(demux_16x1_1_s5), .Clear(Clear), .Q(registrador_8bits_6_q));
  REGISTRADOR_8BITS registrador_8bits_7 (
    .Data(Write_Data), .Clock(demux_16x1_1_s6), .Clear(Clear), .Q(registrador_8bits_7_q));
  REGISTRADOR_8BITS registrador_8bits_8 (
    .Data(Write_Data), .Clock(demux_16x1_1_s7), .Clear(Clear), .Q(registrador_8bits_8_q));
  REGISTRADOR_8BITS registrador_8bits_9 (
    .Data(Write_Data), .Clock(demux_16x1_1_s8), .Clear(Clear), .Q(registrador_8bits_9_q));
  REGISTRADOR_8BITS registrador_8bits_10 (
    .Data(Write_Data), .Clock(demux_16x1_1_s9), .Clear(Clear), .Q(registrador_8bits_10_q));
  REGISTRADOR_8BITS registrador_8bits_11 (
    .Data(Write_Data), .Clock(demux_16x1_1_s10), .Clear(Clear), .Q(registrador_8bits_11_q));
  REGISTRADOR_8BITS registrador_8bits_12 (
    .Data(Write_Data), .Clock(demux_16x1_1_s11), .Clear(Clear), .Q(registrador_8bits_12_q));
  REGISTRADOR_8BITS registrador_8bits_13 (
    .Data(Write_Data), .Clock(demux_16x1_1_s12), .Clear(Clear), .Q(registrador_8bits_13_q));
  REGISTRADOR_8BITS registrador_8bits_14 (
    .Data(Write_Data), .Clock(demux_16x1_1_s13), .Clear(Clear), .Q(registrador_8bits_14_q));
  REGISTRADOR_8BITS registrador_8bits_15 (
    .Data(Write_Data), .Clock(demux_16x1_1_s14), .Clear(Clear), .Q(registrador_8bits_15_q));
  REGISTRADOR_8BITS registrador_8bits_16 (
    .Data(Write_Data), .Clock(demux_16x1_1_s15), .Clear(Clear), .Q(registrador_8bits_16_q));
  MUX_16X1_8BITS mux_16x1_8bits_1 (
    .A0(registrador_8bits_1_q), .A1(registrador_8bits_2_q), .A2(registrador_8bits_3_q),
    .A3(registrador_8bits_4_q), .A4(registrador_8bits_5_q), .A5(registrador_8bits_6_q),
    .A6(registrador_8bits_7_q), .A7(registrador_8bits_8_q), .A8(registrador_8bits_9_q),
    .A9(registrador_8bits_10_q), .A10(registrador_8bits_11_q), .A11(registrador_8bits_12_q),
    .A12(registrador_8bits_13_q), .A13(registrador_8bits_14_q), .A14(registrador_8bits_15_q),
    .A15(registrador_8bits_16_q), .Select(Add_Reg1), .Enable(Able_Read1), .out_19(Read_Reg1));
  MUX_16X1_8BITS mux_16x1_8bits_2 (
    .A0(registrador_8bits_1_q), .A1(registrador_8bits_2_q), .A2(registrador_8bits_3_q),
    .A3(registrador_8bits_4_q), .A4(registrador_8bits_5_q), .A5(registrador_8bits_6_q),
    .A6(registrador_8bits_7_q), .A7(registrador_8bits_8_q), .A8(registrador_8bits_9_q),
    .A9(registrador_8bits_10_q), .A10(registrador_8bits_11_q), .A11(registrador_8bits_12_q),
    .A12(registrador_8bits_13_q), .A13(registrador_8bits_14_q), .A14(registrador_8bits_15_q),
    .A15(registrador_8bits_16_q), .Select(Add_Reg2), .Enable(Able_Reg2), .out_19(Read_Reg2));
endmodule

module FF_JK (
  input  Preset,
  input  J,
  input  Clock,
  input  K,
  input  Clear,
  output Q,
  output nQ
);

  wire nand_1_out, nand_2_out, nand_3_out, nand_4_out, nand_5_out, nand_6_out, not_1_out, not_2_out,
       not_3_out;

  nand nand_1 (nand_1_out, J, nQ, Clock);
  not not_1 (not_1_out, Clock);
  nand nand_2 (nand_2_out, Clock, Q, K);
  not not_2 (not_2_out, Preset);
  not not_3 (not_3_out, Clear);
  nand nand_3 (nand_3_out, not_2_out, nand_1_out, nand_4_out);
  nand nand_4 (nand_4_out, nand_3_out, nand_2_out, not_3_out);
  nand nand_5 (nand_5_out, not_3_out, nand_3_out, not_1_out);
  nand nand_6 (nand_6_out, not_1_out, nand_4_out, not_2_out);
  nand nand_7 (Q, not_2_out, nand_5_out, nQ);
  nand nand_8 (nQ, Q, nand_6_out, not_3_out);
endmodule

module FF_D (
  input  D,
  input  CLK,
  input  _1,
  input  _0,
  output out_5,
  output out_6
);

  wire not_1_out;

  not not_1 (not_1_out, D);
  FF_JK ff_jk_1 (.Preset(_1), .J(D), .Clock(CLK), .K(not_1_out), .Clear(_0), .Q(out_5), .nQ(out_6));
endmodule

module REGISTRADOR_8BITS (
  input  [7:0] Data,
  input  Clock,
  input  Clear,
  output [7:0] Q
);

  FF_D ff_d_1 (.D(Data[0]), .CLK(Clock), .out_5(Q[0]), ._1(1'b0), ._0(Clear));  // open: out_6
  FF_D ff_d_2 (.D(Data[1]), .CLK(Clock), .out_5(Q[1]), ._1(1'b0), ._0(Clear));  // open: out_6
  FF_D ff_d_3 (.D(Data[2]), .CLK(Clock), .out_5(Q[2]), ._1(1'b0), ._0(Clear));  // open: out_6
  FF_D ff_d_4 (.D(Data[3]), .CLK(Clock), .out_5(Q[3]), ._1(1'b0), ._0(Clear));  // open: out_6
  FF_D ff_d_5 (.D(Data[4]), .CLK(Clock), .out_5(Q[4]), ._1(1'b0), ._0(Clear));  // open: out_6
  FF_D ff_d_6 (.D(Data[5]), .CLK(Clock), .out_5(Q[5]), ._1(1'b0), ._0(Clear));  // open: out_6
  FF_D ff_d_7 (.D(Data[6]), .CLK(Clock), .out_5(Q[6]), ._1(1'b0), ._0(Clear));  // open: out_6
  FF_D ff_d_8 (.D(Data[7]), .CLK(Clock), .out_5(Q[7]), ._1(1'b0), ._0(Clear));  // open: out_6
endmodule

module DEMUX_8X1 (
  input  D,
  input  Load,
  input  [2:0] Select,
  output S,
  output S_2,
  output S_3,
  output S_4,
  output S_5,
  output S_6,
  output S_7,
  output S_8
);

  wire and_1_out, not_1_out, not_2_out, not_3_out, not_4_out, not_5_out, not_6_out, not_7_out, not_8_out,
       not_9_out, not_10_out, not_11_out, not_12_out;

  and and_1 (and_1_out, D, Load);
  not not_1 (not_1_out, Select[0]);
  not not_2 (not_2_out, Select[1]);
  not not_3 (not_3_out, Select[2]);
  not not_4 (not_4_out, Select[1]);
  not not_5 (not_5_out, Select[2]);
  not not_6 (not_6_out, Select[0]);
  not not_7 (not_7_out, Select[2]);
  not not_8 (not_8_out, Select[2]);
  not not_9 (not_9_out, Select[0]);
  not not_10 (not_10_out, Select[1]);
  not not_11 (not_11_out, Select[1]);
  not not_12 (not_12_out, Select[0]);
  and _0 (S, not_1_out, not_2_out, not_3_out, and_1_out);
  and _1 (S_2, Select[0], not_4_out, not_5_out, and_1_out);
  and _2 (S_3, not_6_out, Select[1], not_7_out, and_1_out);
  and _3 (S_4, Select[0], Select[1], not_8_out, and_1_out);
  and _4 (S_5, not_9_out, not_10_out, Select[2], and_1_out);
  and _5 (S_6, Select[0], not_11_out, Select[2], and_1_out);
  and _6 (S_7, not_12_out, Select[1], Select[2], and_1_out);
  and _7 (S_8, Select[0], Select[1], Select[2], and_1_out);
endmodule

module MUX_2X1 (
  input  I0,
  input  I1,
  input  Load,
  input  Select,
  output out_5
);

  wire and_1_out, and_2_out, not_1_out, or_1_out;

  not not_1 (not_1_out, Select);
  and and_1 (and_1_out, not_1_out, I0);
  and and_2 (and_2_out, I1, Select);
  or or_1 (or_1_out, and_1_out, and_2_out);
  and and_3 (out_5, or_1_out, Load);
endmodule

module MUX_2X1_8BITS (
  input  [7:0] in_1,
  input  [7:0] in_2,
  input  Select,
  input  Load,
  output [7:0] out_5
);

  MUX_2X1 mux_2x1_1 (.I0(in_1[0]), .I1(in_2[0]), .Select(Select), .out_5(out_5[0]), .Load(Load));
  MUX_2X1 mux_2x1_2 (.I0(in_1[1]), .I1(in_2[1]), .Select(Select), .out_5(out_5[1]), .Load(Load));
  MUX_2X1 mux_2x1_3 (.I0(in_1[2]), .I1(in_2[2]), .Select(Select), .out_5(out_5[2]), .Load(Load));
  MUX_2X1 mux_2x1_4 (.I0(in_1[3]), .I1(in_2[3]), .Select(Select), .out_5(out_5[3]), .Load(Load));
  MUX_2X1 mux_2x1_5 (.I0(in_1[4]), .I1(in_2[4]), .Select(Select), .out_5(out_5[4]), .Load(Load));
  MUX_2X1 mux_2x1_6 (.I0(in_1[5]), .I1(in_2[5]), .Select(Select), .out_5(out_5[5]), .Load(Load));
  MUX_2X1 mux_2x1_7 (.I0(in_1[6]), .I1(in_2[6]), .Select(Select), .out_5(out_5[6]), .Load(Load));
  MUX_2X1 mux_2x1_8 (.I0(in_1[7]), .I1(in_2[7]), .Select(Select), .out_5(out_5[7]), .Load(Load));
endmodule

module MUX_4X1_8BITS (
  input  [7:0] A0,
  input  [7:0] A1,
  input  [7:0] A2,
  input  [7:0] A3,
  input  [1:0] Select,
  input  Load,
  output [7:0] Saida
);

  wire [7:0] mux_2x1_8bits_1_out_5, mux_2x1_8bits_2_out_5;

  MUX_2X1_8BITS mux_2x1_8bits_1 (.in_1(A0), .in_2(A1), .Select(Select[0]), .out_5(mux_2x1_8bits_1_out_5), .Load(Load));
  MUX_2X1_8BITS mux_2x1_8bits_2 (.in_1(A2), .in_2(A3), .Select(Select[0]), .out_5(mux_2x1_8bits_2_out_5), .Load(Load));
  MUX_2X1_8BITS mux_2x1_8bits_3 (
    .in_1(mux_2x1_8bits_1_out_5), .in_2(mux_2x1_8bits_2_out_5), .Select(Select[1]), .out_5(Saida), .Load(Load));
endmodule

module MUX_8X1_8BITS (
  input  [7:0] A0,
  input  [7:0] A1,
  input  [7:0] A2,
  input  [7:0] A3,
  input  [7:0] A4,
  input  [7:0] A5,
  input  [7:0] A6,
  input  [7:0] A7,
  input  [2:0] Seletor,
  input  Load,
  output [7:0] Saida
);

  wire [7:0] mux_4x1_8bits_1_saida, mux_4x1_8bits_2_saida;

  MUX_4X1_8BITS mux_4x1_8bits_1 (
    .A0(A0), .A1(A1), .A2(A2), .A3(A3), .Select(Seletor[1:0]), .Saida(mux_4x1_8bits_1_saida), .Load(Load));
  MUX_4X1_8BITS mux_4x1_8bits_2 (
    .A0(A4), .A1(A5), .A2(A6), .A3(A7), .Select(Seletor[1:0]), .Saida(mux_4x1_8bits_2_saida), .Load(Load));
  MUX_2X1_8BITS mux_2x1_8bits_1 (
    .in_1(mux_4x1_8bits_1_saida), .in_2(mux_4x1_8bits_2_saida), .Select(Seletor[2]), .out_5(Saida),
    .Load(Load));
endmodule

module MUX_16X1_8BITS (
  input  [7:0] A0,
  input  [7:0] A1,
  input  [7:0] A2,
  input  [7:0] A3,
  input  [7:0] A4,
  input  [7:0] A5,
  input  [7:0] A6,
  input  [7:0] A7,
  input  [7:0] A8,
  input  [7:0] A9,
  input  [7:0] A10,
  input  [7:0] A11,
  input  [7:0] A12,
  input  [7:0] A13,
  input  [7:0] A14,
  input  [7:0] A15,
  input  [3:0] Select,
  input  Enable,
  output [7:0] out_19
);

  wire [7:0] mux_8x1_8bits_1_saida, mux_8x1_8bits_2_saida;

  MUX_8X1_8BITS mux_8x1_8bits_1 (
    .A0(A0), .A1(A1), .A2(A2), .A3(A3), .A4(A4), .A5(A5), .A6(A6), .A7(A7), .Seletor(Select[2:0]),
    .Saida(mux_8x1_8bits_1_saida), .Load(Enable));
  MUX_8X1_8BITS mux_8x1_8bits_2 (
    .A0(A8), .A1(A9), .A2(A10), .A3(A11), .A4(A12), .A5(A13), .A6(A14), .A7(A15), .Seletor(Select[2:0]),
    .Saida(mux_8x1_8bits_2_saida), .Load(Enable));
  MUX_2X1_8BITS mux_2x1_8bits_1 (
    .in_1(mux_8x1_8bits_1_saida), .in_2(mux_8x1_8bits_2_saida), .Select(Select[3]), .out_5(out_19),
    .Load(Enable));
endmodule

module DEMUX_16X1 (
  input  Data,
  input  [3:0] Select,
  input  in_3,
  output S0,
  output S1,
  output S2,
  output S3,
  output S4,
  output S5,
  output S6,
  output S7,
  output S8,
  output S9,
  output S10,
  output S11,
  output S12,
  output S13,
  output S14,
  output S15
);

  wire demux_2x1_1_s0, demux_2x1_1_s1;

  DEMUX_2X1 demux_2x1_1 (.D(Data), .Enable(in_3), .Select(Select[0]), .S0(demux_2x1_1_s0), .S1(demux_2x1_1_s1));
  DEMUX_8X1 demux_8x1_1 (
    .D(demux_2x1_1_s0), .Select(Select[3:1]), .S(S0), .Load(in_3), .S_2(S1), .S_3(S2), .S_4(S3), .S_5(S4),
    .S_6(S5), .S_7(S6), .S_8(S7));
  DEMUX_8X1 demux_8x1_2 (
    .D(demux_2x1_1_s1), .Select(Select[3:1]), .S(S8), .Load(in_3), .S_2(S9), .S_3(S10), .S_4(S11), .S_5(S12),
    .S_6(S13), .S_7(S14), .S_8(S15));
endmodule

module DEMUX_2X1 (
  input  D,
  input  Enable,
  input  Select,
  output S0,
  output S1
);

  wire and_1_out, not_1_out;

  and and_1 (and_1_out, D, Enable);
  not not_1 (not_1_out, Select);
  and and_2 (S0, not_1_out, and_1_out);
  and and_3 (S1, and_1_out, Select);
endmodule
