// Logisim project 9-DETECTOR_SEQUENCIA_101.circ as structural Verilog: 3 circuits, main circuit DETECTOR_SEQUENCIA_101
module DETECTOR_SEQUENCIA_101 (
  input  Fluxo_Entrada,
  input  Preset,
  input  Clear,
  output Resultado,
  output [2:0] Saida
);

  wire Clock_out, not_1_out;

  Clock Clock (.out(Clock_out));
  FF_D ff_d_1 (.Data(Fluxo_Entrada), .CLK(Clock_out), .Q(Saida[0]), .Preset(Preset), .Clear(Clear));  // open: nQ
  and and_1 (Resultado, Saida[0], not_1_out, Saida[2]);
  not not_1 (not_1_out, Saida[1]);
  FF_D ff_d_2 (.Data(Saida[0]), .CLK(Clock_out), .Q(Saida[1]), .Preset(Preset), .Clear(Clear));  // open: nQ
  FF_D ff_d_3 (.Data(Saida[1]), .CLK(Clock_out), .Q(Saida[2]), .Preset(Preset), .Clear(Clear));  // open: nQ
endmodule

module FF_JK (
  input  Preset,
  input  J,
  input  CLK,
  input  K,
  input  Clear,
  output Q,
  output nQ
);

  wire nand_1_out, nand_2_out, nand_3_out, nand_4_out, nand_5_out, nand_6_out, not_1_out, not_2_out,
       not_3_out;

  not not_1 (not_1_out, Preset);
  nand nand_1 (nand_1_out, nQ, J, CLK);
  not not_2 (not_2_out, CLK);
  nand nand_2 (nand_2_out, CLK, K, Q);
  not not_3 (not_3_out, Clear);
  nand nand_3 (nand_3_out, not_1_out, nand_1_out, nand_4_out);
  nand nand_4 (nand_4_out, nand_3_out, nand_2_out, not_3_out);
  nand nand_5 (nand_5_out, not_3_out, nand_3_out, not_2_out);
  nand nand_6 (nand_6_out, not_2_out, nand_4_out, not_1_out);
  nand nand_7 (Q, not_1_out, nand_5_out, nQ);
  nand nand_8 (nQ, Q, nand_6_out, not_3_out);
endmodule

module FF_D (
  input  Data,
  input  CLK,
  input  Preset,
  input  Clear,
  output Q,
  output nQ
);

  wire not_1_out;

  not not_1 (not_1_out, Data);
  FF_JK ff_jk_1 (.Preset(Preset), .J(Data), .CLK(CLK), .K(not_1_out), .Clear(Clear), .Q(Q), .nQ(nQ));
endmodule
